# Fritzing sketch 01-led (saved by Fritzing 0.9.4)
breadboards: 1

parts:
  Bauteil1 = Arduino Uno (Rev3)
  R1 = Resistor [tolerance=±5% resistance=100 package="0603 [SMD]"]
  LED1 = smd LED [color="Red (633nm)" package="0603 [SMD]"]

nets:
  N1: Bauteil1.D10_PWM/SS, R1.Pin_1
  N2: Bauteil1.GND, LED1.cathode
  N3: R1.Pin_0, LED1.anode
