# Fritzing sketch 02-potentiometer (saved by Fritzing 0.9.4)
breadboards: 1

parts:
  Bauteil1 = Arduino Uno (Rev3)
  R2 = Trimmer Potentiometer [maximum_resistance=10kΩ package=THT]

nets:
  N1: Bauteil1.A0, R2.wiper
  N2: Bauteil1.5V, R2.leg2
  N3: Bauteil1.GND, R2.leg1
