# Fritzing sketch 03-led-potentiometer (saved by Fritzing 0.9.4)
breadboards: 1

parts:
  Bauteil1 = Arduino Uno (Rev3)
  R1 = Resistor [tolerance=±5% resistance=100 package="0603 [SMD]"]
  LED1 = smd LED [color="Red (633nm)" package="0603 [SMD]"]
  R2 = Trimmer Potentiometer [maximum_resistance=10kΩ package=THT]

nets:
  N1: Bauteil1.A0, R2.wiper
  N2: Bauteil1.D10_PWM/SS, R1.Pin_1
  N3: Bauteil1.5V, R2.leg2
  N4: Bauteil1.GND, LED1.cathode, R2.leg1
  N5: R1.Pin_0, LED1.anode
